# Fritzing sketch Schéma (saved by Fritzing 0.9.3b)
breadboards: 1

parts:
  LED1 = LED - 5mm [color="Yellow (595nm)" package="5 mm [THT]"]
  LED2 = LED - 5mm [color="Yellow (595nm)" package="5 mm [THT]"]
  LED3 = LED - 5mm [color="Red (633nm)" package="5 mm [THT]"]
  Part1 = Arduino Uno (Rev3) - ICSP
  R2 = Resistor [tolerance=±5% resistance=220 package=THT]
  R3 = Resistor [tolerance=±5% resistance=220 package=THT]
  R4 = Resistor [tolerance=±5% resistance=220 package=THT]
  S1 = Pushbutton [package=THT]
  S2 = Pushbutton [package=THT]
  S3 = Pushbutton [package=THT]
  R5 = Rotary Potentiometer (Small) [maximum_resistance=100kΩ package=THT]
  R6 = Resistor [tolerance=±5% resistance=2.2k package=THT]
  R7 = Resistor [tolerance=±5% resistance=2.2k package=THT]
  R8 = Resistor [tolerance=±5% resistance=2.2k package=THT]

nets:
  N1: LED1.cathode, R4.Pin_1
  N2: LED1.anode, Part1.D12/MISO
  N3: LED2.cathode, R3.Pin_1
  N4: LED2.anode, Part1.D11_PWM/MOSI
  N5: LED3.cathode, R2.Pin_1
  N6: LED3.anode, Part1.D10_PWM/SS
  N7: Part1.A0, R5.wiper
  N8: Part1.5V, S1.leg1, S2.leg1, S3.leg1, R5.leg2
  N9: Part1.GND, R2.Pin_0, R3.Pin_0, R4.Pin_0, R5.leg1, R6.Pin_1, R7.Pin_1, R8.Pin_1
  N10: Part1.D5_PWM, S3.leg0, R8.Pin_0
  N11: Part1.D6_PWM, S1.leg0, R7.Pin_0
  N12: Part1.D7, S2.leg0, R6.Pin_0
